# Fritzing sketch printplaatRaspberry (saved by Fritzing 0.9.3b)
circuit board: 6.04455cm x 4.62293cm
breadboards: 1

parts:
  Raspberry_Pi_1 = Raspberry Pi 3 [part_number=RPI-3-V1.2]
  LED1 = LED - 5mm [color="Red (633nm)" package="5 mm [THT]"]
  LED2 = LED - 5mm [color="Red (633nm)" package="5 mm [THT]"]
  LED3 = LED - 5mm [color="Red (633nm)" package="5 mm [THT]"]
  S1 = SWITCH-MOMENTARY-2 [package=tactile_switch_tall]
  S2 = SWITCH-MOMENTARY-2 [package=tactile_switch_tall]
  S3 = SWITCH-MOMENTARY-2 [package=tactile_switch_tall]

nets:
  3V3: Raspberry_Pi_1.3v3, Raspberry_Pi_1.3V3
  N1: Raspberry_Pi_1.GND, LED1.cathode, LED2.cathode, LED3.cathode, S1.1, S2.1, S3.1
  N2: Raspberry_Pi_1.GPIO10, LED3.anode
  N3: Raspberry_Pi_1.GPIO9, LED2.anode
  N4: Raspberry_Pi_1.GPIO11, LED1.anode
  N5: Raspberry_Pi_1.GPIO7, S3.2
  N6: Raspberry_Pi_1.GPIO25, S2.2
  N7: Raspberry_Pi_1.GPIO23, S1.2
